# Fritzing sketch AlarmClock (saved by Fritzing 1.0.8)

parts:
  A1 = Raspberry Pi 5
  Part1 = SPI OLED Monochrome 128x64 0.96 inch
  Part2 = 24 NeoPixel Ring [part_number=1586]
  Part3 = 16 NeoPixel Ring [part_number=1463]
  Part5 = Adafruit TSL2591 [part_number="Adafruit #1980"]
  S1 = Round Pushbutton

nets:
  3V3: A1.3V3, Part1.VDD, Part5.VIN
  VDD: A1.5V, Part2.VDD, Part3.VDD
  N1: A1.GPIO2, Part5.SDA
  N2: A1.GPIO3, Part5.SCL
  GND: A1.GND, Part1.GND, Part2.GND, Part3.GND, Part5.GND, S1.leg0
  N3: A1.GPIO24, Part1.DC
  N4: A1.GPIO10, Part1.SDA
  N5: A1.GPIO25, Part1.RES
  N6: A1.GPIO11, Part1.SCK
  N7: A1.GPIO8, Part1.CS
  N8: A1.GPIO13, S1.leg1
  N9: A1.GPIO20, Part2.IN
  N10: Part2.OUT, Part3.IN

notes:
  ssd1331 LCD
  Button Out -> Ground
  WS2812
  LEDS

custom parts:
  Raspberry Pi 5: The RPi5, a faster version of the awesome Raspberry Pi4B ARM Board with 40 pin gpio.
  SPI OLED Monochrome 128x64 0.96 inch: Unknown 128x64 0.96 inch 128x64 SPI Monochrome OLED display
  24 NeoPixel Ring: 24 ultra bright smart LED NeoPixels are arranged in a circle with 2.6" (66mm) outer diameter. The rings are 'chainable' - connect the output pin of one to the input pin of another. Use only one microcontroller pin to control as many as you can chain together! Each LED is addressable as the driver chip is inside the LED. Each one has ~18mA constant current drive so the color will be very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
  16 NeoPixel Ring: 16 ultra bright smart LED NeoPixels are arranged in a circle with 1.75" (44.5mm) outer diameter. The rings are 'chainable' - connect the output pin of one to the input pin of another. Use only one microcontroller pin to control as many as you can chain together! Each LED is addressable as the driver chip is inside the LED. Each one has ~18mA constant current drive so the color will be very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
  Adafruit TSL2591: When the future is dazzlingly-bright, this ultra-high-range luminosity sensor will help you measure it. The TSL2591 luminosity sensor is an advanced digital light sensor, ideal for use in a wide range of light situations. Compared to low cost CdS cells, this sensor is more precise, allowing for exact lux calculations and can be configured for different gain/timing ranges to detect light ranges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
